# Fritzing sketch Sensors (saved by Fritzing 0.5.2b)
breadboards: 2

parts:
  2x16_HD44780-controlled_LCD = LCD screen
  Netduino1 = Netduino Plus
  10K_Pot_to_control_brightness = Trimmer Potentiometer [package=THT]
  330Ω = Resistor [resistance=330 package=THT]
  CdS_photoresistor = Photocell (LDR) [package=THT]
  1kΩ = Resistor [resistance=1k package=THT]
  TMP36_Temp_Sensor = DIP - 4 pins

nets:
  VSS: 2x16_HD44780-controlled_LCD.VSS, 2x16_HD44780-controlled_LCD.R/W, 2x16_HD44780-controlled_LCD.LED-, Netduino1.GND, 10K_Pot_to_control_brightness.leg1, 1kΩ.Pin_1, TMP36_Temp_Sensor.connector0
  VDD: 2x16_HD44780-controlled_LCD.VDD, Netduino1.+5V, 10K_Pot_to_control_brightness.leg2, 330Ω.Pin_0, CdS_photoresistor.pin_1
  N1: 2x16_HD44780-controlled_LCD.V0, 10K_Pot_to_control_brightness.wiper
  N2: 2x16_HD44780-controlled_LCD.RS, Netduino1.D12_MISO
  N3: 2x16_HD44780-controlled_LCD.E, Netduino1.D11_MOSI
  N4: 2x16_HD44780-controlled_LCD.DB0, Netduino1.D9_PWM2
  N5: 2x16_HD44780-controlled_LCD.DB1, Netduino1.D8_CTS1
  N6: 2x16_HD44780-controlled_LCD.DB2, Netduino1.D7_RTS1
  N7: 2x16_HD44780-controlled_LCD.DB3, Netduino1.D6_PWM1
  N8: 2x16_HD44780-controlled_LCD.DB4, Netduino1.D5_PWM0
  N9: 2x16_HD44780-controlled_LCD.DB5, Netduino1.D4_CS0
  N10: 2x16_HD44780-controlled_LCD.DB6, Netduino1.D3_TX1
  N11: 2x16_HD44780-controlled_LCD.DB7, Netduino1.D2_RX1
  N12: 2x16_HD44780-controlled_LCD.LED+, 330Ω.Pin_1
  N13: Netduino1.3V3, TMP36_Temp_Sensor.connector2
  N14: Netduino1.A0, CdS_photoresistor.pin_0, 1kΩ.Pin_0
  N15: Netduino1.A1, TMP36_Temp_Sensor.connector1

notes:
  Actually 5-band:
  orange-orange-black-black-brown
